// Logisim project Cpu.circ as structural Verilog: 18 circuits, main circuit Main
module Main (
  input  Clock,
  input  Reset,
  output [11:0] PC_Value
);

  wire ALUSrc, comparator_1_eq, IRWrite, MemToReg, MemWrite, PCSrc, PCWrite, RegDst, RegWrite, Zero;
  wire [2:0] ALUOp;
  wire [3:0] Dest_Reg, multiplexer_1_out, multiplexer_2_out, Src1_Reg;
  wire [4:0] Opcode, Src2_Imm;
  wire [11:0] _12_bit_Offset, adder_1_out, adder_2_out, multiplexer_3_out;
  wire [17:0] ALU_Result, ALUOut_q, multiplexer_4_out, oData1, oData2, ram_1_data, register_file_1_r0,
       register_file_1_r1, register_file_1_r2, register_file_1_r3, register_file_1_r4, register_file_1_r5,
       register_file_1_r6, register_file_1_r7, register_file_1_r8, register_file_1_r9, register_file_1_r10,
       register_file_1_r11, register_file_1_r12, register_file_1_r13, register_file_1_r14,
       register_file_1_r15, rom_1_data, wData;
  wire [17:12] bit_extender_1_out;

  Comparator #(.width(5)) comparator_1 (.a(Opcode), .b(5'b01011), .eq(comparator_1_eq));  // open: gt, lt
  Multiplexer #(.width(4)) multiplexer_1 (
    .in0(Dest_Reg), .in1(4'b1111), .out(multiplexer_1_out), .sel(RegDst));  // open: en
  Adder #(.width(12)) adder_1 (.a(PC_Value), .b(12'h1), .out(adder_1_out));  // open: cin, cout
  Adder #(.width(12)) adder_2 (.a(adder_1_out), .b(_12_bit_Offset), .out(adder_2_out));  // open: cin, cout
  Multiplexer #(.width(4)) multiplexer_2 (
    .in0(Src2_Imm[3:0]), .in1(Dest_Reg), .out(multiplexer_2_out), .sel(comparator_1_eq));  // open: en
  Register_File register_file_1 (
    .R0(register_file_1_r0), .R1(register_file_1_r1), .R2(register_file_1_r2), .rReg1(Src1_Reg),
    .R3(register_file_1_r3), .oData1(oData1), .R4(register_file_1_r4), .R5(register_file_1_r5),
    .oData2(oData2), .R6(register_file_1_r6), .rReg2(multiplexer_2_out), .wData(wData),
    .R7(register_file_1_r7), .R8(register_file_1_r8), .R9(register_file_1_r9), .R10(register_file_1_r10),
    .wReg(multiplexer_1_out), .R11(register_file_1_r11), .R12(register_file_1_r12),
    .R13(register_file_1_r13), .R14(register_file_1_r14), .R15(register_file_1_r15), .WE(RegWrite),
    .Clock(Clock), .reset(Reset));
  Multiplexer #(.width(12)) multiplexer_3 (
    .in0(adder_1_out), .in1(adder_2_out), .out(multiplexer_3_out), .sel(PCSrc));  // open: en
  Register #(.width(12)) register_1 (.D(multiplexer_3_out), .en(PCWrite), .Q(PC_Value), .clk(Clock), .clr(Reset));
  // Probe on register_file_1_r0
  // Probe on register_file_1_r1
  // Probe on register_file_1_r2
  // Probe on register_file_1_r3
  // Probe on register_file_1_r4
  // Probe on register_file_1_r5
  // Probe on register_file_1_r6
  // Probe on register_file_1_r7
  // Probe on register_file_1_r8
  // Probe on register_file_1_r9
  // Probe on register_file_1_r10
  // Probe on register_file_1_r11
  // Probe on register_file_1_r12
  // Probe on register_file_1_r13
  // Probe on register_file_1_r14
  // Probe on register_file_1_r15
  ROM #(.addrWidth(12), .dataWidth(18)) rom_1 (.addr(PC_Value), .data(rom_1_data), .sel(1'b1));
  Register #(.width(18)) IR (
    .D(rom_1_data), .en(IRWrite), .Q({Opcode, Dest_Reg, Src1_Reg, Src2_Imm}), .clk(Clock), .clr(Reset));
  assign {bit_extender_1_out, _12_bit_Offset} = {{13{Src2_Imm[4]}}, Src2_Imm};  // Bit_Extender bit_extender_1
  Control_Unit control_unit_1 (
    .Opcode(Opcode), .Zero(Zero), .Clock(Clock), .Reset(Reset), .PCWrite(PCWrite), .IRWrite(IRWrite),
    .RegWrite(RegWrite), .MemWrite(MemWrite), .MemToReg(MemToReg), .ALUSrc(ALUSrc), .RegDst(RegDst),
    .PCSrc(PCSrc), .ALUOp(ALUOp));
  Multiplexer #(.width(18)) multiplexer_4 (
    .in0(oData2), .in1({bit_extender_1_out, _12_bit_Offset}), .out(multiplexer_4_out), .sel(ALUSrc));  // open: en
  ALU_18bit alu_18bit_1 (
    .Input_A(oData1), .Input_B(multiplexer_4_out), .ALU_Op(ALUOp), .Result(ALU_Result), .Zero_Flag(Zero));
  Register #(.width(18)) ALUOut (.D(ALU_Result), .en(1'b1), .Q(ALUOut_q), .clk(Clock));  // open: clr
  RAM #(.addrWidth(12), .dataWidth(18), .bus("separate")) ram_1 (
    .addr(ALUOut_q[11:0]), .din(oData2), .data(ram_1_data), .str(MemWrite), .sel(1'b1), .clk(Clock),
    .ld(1'b1), .clr(Reset));
  Multiplexer #(.width(18)) multiplexer_5 (.in0(ALUOut_q), .in1(ram_1_data), .out(wData), .sel(MemToReg));  // open: en

  // Notes on the sheet:
  //   PC (12-bit)
  //   Instruction Memory (18b Data, 12b Addr)
  //   contents of rom_1 (hex, n*v repeats v):
  //   c205 c40a 622 16600 18000
endmodule

// RegFile
module Register_File (
  input  [3:0] rReg1,
  input  [3:0] rReg2,
  input  [17:0] wData,
  input  [3:0] wReg,
  input  WE,
  input  Clock,
  input  reset,
  output [17:0] R0,
  output [17:0] R1,
  output [17:0] R2,
  output [17:0] R3,
  output [17:0] oData1,
  output [17:0] R4,
  output [17:0] R5,
  output [17:0] oData2,
  output [17:0] R6,
  output [17:0] R7,
  output [17:0] R8,
  output [17:0] R9,
  output [17:0] R10,
  output [17:0] R11,
  output [17:0] R12,
  output [17:0] R13,
  output [17:0] R14,
  output [17:0] R15
);

  wire and_1_out, and_2_out, and_3_out, and_4_out, and_5_out, and_6_out, and_7_out, and_8_out, and_9_out,
       and_10_out, and_11_out, and_12_out, and_13_out, and_14_out, and_15_out, and_16_out, decoder_1_out0,
       decoder_1_out1, decoder_1_out2, decoder_1_out3, decoder_1_out4, decoder_1_out5, decoder_1_out6,
       decoder_1_out7, decoder_1_out8, decoder_1_out9, decoder_1_out10, decoder_1_out11, decoder_1_out12,
       decoder_1_out13, decoder_1_out14, decoder_1_out15, decoder_2_out0, decoder_2_out1, decoder_2_out2,
       decoder_2_out3, decoder_2_out4, decoder_2_out5, decoder_2_out6, decoder_2_out7, decoder_2_out8,
       decoder_2_out9, decoder_2_out10, decoder_2_out11, decoder_2_out12, decoder_2_out13, decoder_2_out14,
       decoder_2_out15, decoder_3_out0, decoder_3_out1, decoder_3_out2, decoder_3_out3, decoder_3_out4,
       decoder_3_out5, decoder_3_out6, decoder_3_out7, decoder_3_out8, decoder_3_out9, decoder_3_out10,
       decoder_3_out11, decoder_3_out12, decoder_3_out13, decoder_3_out14, decoder_3_out15;

  Decoder #(.select(4), .enable("false")) decoder_1 (
    .out0(decoder_1_out0), .out1(decoder_1_out1), .out2(decoder_1_out2), .out3(decoder_1_out3),
    .out4(decoder_1_out4), .out5(decoder_1_out5), .out6(decoder_1_out6), .out7(decoder_1_out7),
    .out8(decoder_1_out8), .out9(decoder_1_out9), .out10(decoder_1_out10), .out11(decoder_1_out11),
    .out12(decoder_1_out12), .out13(decoder_1_out13), .out14(decoder_1_out14), .out15(decoder_1_out15),
    .sel(rReg1));
  Decoder #(.select(4), .enable("false")) decoder_2 (
    .out0(decoder_2_out0), .out1(decoder_2_out1), .out2(decoder_2_out2), .out3(decoder_2_out3),
    .out4(decoder_2_out4), .out5(decoder_2_out5), .out6(decoder_2_out6), .out7(decoder_2_out7),
    .out8(decoder_2_out8), .out9(decoder_2_out9), .out10(decoder_2_out10), .out11(decoder_2_out11),
    .out12(decoder_2_out12), .out13(decoder_2_out13), .out14(decoder_2_out14), .out15(decoder_2_out15),
    .sel(rReg2));
  Decoder #(.select(4), .enable("false")) decoder_3 (
    .out0(decoder_3_out0), .out1(decoder_3_out1), .out2(decoder_3_out2), .out3(decoder_3_out3),
    .out4(decoder_3_out4), .out5(decoder_3_out5), .out6(decoder_3_out6), .out7(decoder_3_out7),
    .out8(decoder_3_out8), .out9(decoder_3_out9), .out10(decoder_3_out10), .out11(decoder_3_out11),
    .out12(decoder_3_out12), .out13(decoder_3_out13), .out14(decoder_3_out14), .out15(decoder_3_out15),
    .sel(wReg));
  and and_1 (and_1_out, decoder_3_out0, WE);
  and and_2 (and_2_out, decoder_3_out1, WE);
  and and_3 (and_3_out, decoder_3_out2, WE);
  and and_4 (and_4_out, decoder_3_out3, WE);
  and and_5 (and_5_out, decoder_3_out4, WE);
  and and_6 (and_6_out, decoder_3_out5, WE);
  and and_7 (and_7_out, decoder_3_out6, WE);
  and and_8 (and_8_out, decoder_3_out7, WE);
  and and_9 (and_9_out, decoder_3_out8, WE);
  and and_10 (and_10_out, decoder_3_out9, WE);
  and and_11 (and_11_out, decoder_3_out10, WE);
  and and_12 (and_12_out, decoder_3_out11, WE);
  and and_13 (and_13_out, decoder_3_out12, WE);
  and and_14 (and_14_out, decoder_3_out13, WE);
  and and_15 (and_15_out, decoder_3_out14, WE);
  and and_16 (and_16_out, decoder_3_out15, WE);
  Register #(.width(18)) register_1 (.D(wData), .en(and_1_out), .Q(R0), .clk(Clock), .clr(reset));
  Register #(.width(18)) register_2 (.D(wData), .en(and_2_out), .Q(R1), .clk(Clock), .clr(reset));
  Register #(.width(18)) register_3 (.D(wData), .en(and_3_out), .Q(R2), .clk(Clock), .clr(reset));
  Register #(.width(18)) register_4 (.D(wData), .en(and_4_out), .Q(R3), .clk(Clock), .clr(reset));
  Register #(.width(18)) register_5 (.D(wData), .en(and_5_out), .Q(R4), .clk(Clock), .clr(reset));
  Register #(.width(18)) register_6 (.D(wData), .en(and_6_out), .Q(R5), .clk(Clock), .clr(reset));
  Register #(.width(18)) register_7 (.D(wData), .en(and_7_out), .Q(R6), .clk(Clock), .clr(reset));
  Register #(.width(18)) register_8 (.D(wData), .en(and_8_out), .Q(R7), .clk(Clock), .clr(reset));
  Register #(.width(18)) register_9 (.D(wData), .en(and_9_out), .Q(R8), .clk(Clock), .clr(reset));
  Register #(.width(18)) register_10 (.D(wData), .en(and_10_out), .Q(R9), .clk(Clock), .clr(reset));
  Register #(.width(18)) register_11 (.D(wData), .en(and_11_out), .Q(R10), .clk(Clock), .clr(reset));
  Register #(.width(18)) register_12 (.D(wData), .en(and_12_out), .Q(R11), .clk(Clock), .clr(reset));
  Register #(.width(18)) register_13 (.D(wData), .en(and_13_out), .Q(R12), .clk(Clock), .clr(reset));
  Register #(.width(18)) register_14 (.D(wData), .en(and_14_out), .Q(R13), .clk(Clock), .clr(reset));
  Register #(.width(18)) register_15 (.D(wData), .en(and_15_out), .Q(R14), .clk(Clock), .clr(reset));
  Register #(.width(18)) register_16 (.D(wData), .en(and_16_out), .Q(R15), .clk(Clock), .clr(reset));
  assign oData1 = decoder_1_out0 ? R0 : 18'bz;  // Controlled_Buffer controlled_buffer_1
  assign oData2 = decoder_2_out0 ? R0 : 18'bz;  // Controlled_Buffer controlled_buffer_2
  assign oData1 = decoder_1_out1 ? R1 : 18'bz;  // Controlled_Buffer controlled_buffer_3
  assign oData2 = decoder_2_out1 ? R1 : 18'bz;  // Controlled_Buffer controlled_buffer_4
  assign oData1 = decoder_1_out2 ? R2 : 18'bz;  // Controlled_Buffer controlled_buffer_5
  assign oData2 = decoder_2_out2 ? R2 : 18'bz;  // Controlled_Buffer controlled_buffer_6
  assign oData1 = decoder_1_out3 ? R3 : 18'bz;  // Controlled_Buffer controlled_buffer_7
  assign oData2 = decoder_2_out3 ? R3 : 18'bz;  // Controlled_Buffer controlled_buffer_8
  assign oData1 = decoder_1_out4 ? R4 : 18'bz;  // Controlled_Buffer controlled_buffer_9
  assign oData2 = decoder_2_out4 ? R4 : 18'bz;  // Controlled_Buffer controlled_buffer_10
  assign oData1 = decoder_1_out5 ? R5 : 18'bz;  // Controlled_Buffer controlled_buffer_11
  assign oData2 = decoder_2_out5 ? R5 : 18'bz;  // Controlled_Buffer controlled_buffer_12
  assign oData1 = decoder_1_out6 ? R6 : 18'bz;  // Controlled_Buffer controlled_buffer_13
  assign oData2 = decoder_2_out6 ? R6 : 18'bz;  // Controlled_Buffer controlled_buffer_14
  assign oData1 = decoder_1_out7 ? R7 : 18'bz;  // Controlled_Buffer controlled_buffer_15
  assign oData2 = decoder_2_out7 ? R7 : 18'bz;  // Controlled_Buffer controlled_buffer_16
  assign oData1 = decoder_1_out8 ? R8 : 18'bz;  // Controlled_Buffer controlled_buffer_17
  assign oData2 = decoder_2_out8 ? R8 : 18'bz;  // Controlled_Buffer controlled_buffer_18
  assign oData1 = decoder_1_out9 ? R9 : 18'bz;  // Controlled_Buffer controlled_buffer_19
  assign oData2 = decoder_2_out9 ? R9 : 18'bz;  // Controlled_Buffer controlled_buffer_20
  assign oData1 = decoder_1_out10 ? R10 : 18'bz;  // Controlled_Buffer controlled_buffer_21
  assign oData2 = decoder_2_out10 ? R10 : 18'bz;  // Controlled_Buffer controlled_buffer_22
  assign oData1 = decoder_1_out11 ? R11 : 18'bz;  // Controlled_Buffer controlled_buffer_23
  assign oData2 = decoder_2_out11 ? R11 : 18'bz;  // Controlled_Buffer controlled_buffer_24
  assign oData1 = decoder_1_out12 ? R12 : 18'bz;  // Controlled_Buffer controlled_buffer_25
  assign oData2 = decoder_2_out12 ? R12 : 18'bz;  // Controlled_Buffer controlled_buffer_26
  assign oData1 = decoder_1_out13 ? R13 : 18'bz;  // Controlled_Buffer controlled_buffer_27
  assign oData2 = decoder_2_out13 ? R13 : 18'bz;  // Controlled_Buffer controlled_buffer_28
  assign oData1 = decoder_1_out14 ? R14 : 18'bz;  // Controlled_Buffer controlled_buffer_29
  assign oData2 = decoder_2_out14 ? R14 : 18'bz;  // Controlled_Buffer controlled_buffer_30
  assign oData1 = decoder_1_out15 ? R15 : 18'bz;  // Controlled_Buffer controlled_buffer_31
  assign oData2 = decoder_2_out15 ? R15 : 18'bz;  // Controlled_Buffer controlled_buffer_32
endmodule

// ALU
module ALU_18bit (
  input  [17:0] Input_A,
  input  [17:0] Input_B,
  input  [2:0] ALU_Op,
  output [17:0] Result,
  output Zero_Flag
);

  wire [17:0] adder_1_out, op_2_out, op_3_out, shifter_1_out, shifter_2_out, subtractor_1_out;

  Adder #(.width(18)) adder_1 (.a(Input_A), .b(Input_B), .out(adder_1_out));  // open: cin, cout
  Subtractor #(.width(18)) subtractor_1 (.a(Input_A), .b(Input_B), .out(subtractor_1_out));  // open: bin, bout
  Shifter #(.width(18), .shift("ar")) shifter_1 (.in(Input_A), .\dist (Input_B[4:0]), .out(shifter_1_out));
  assign op_2_out = ~(Input_A & Input_B);  // NAND_Gate op_2, 18 bits wide
  Shifter #(.width(18), .shift("lr")) shifter_2 (.in(Input_A), .\dist (Input_B[4:0]), .out(shifter_2_out));
  assign op_3_out = ~(Input_A | Input_B);  // NOR_Gate op_3, 18 bits wide
  Multiplexer #(.select(3), .width(18), .enable("false")) multiplexer_1 (
    .in0(adder_1_out), .in1(subtractor_1_out), .in2(op_2_out), .in3(op_3_out), .in4(shifter_2_out),
    .in5(shifter_1_out), .out(Result), .sel(ALU_Op));  // open: in6, in7
  Comparator #(.width(18)) comparator_1 (.a(Result), .b({18{1'b0}}), .eq(Zero_Flag));  // open: gt, lt

  // Notes on the sheet:
  //   Inputs
  //   op 5
  //   op 4
  //   Full 18-bit ALU (ADD, SUB, NAND, NOR, SRL, SRA)
  //   Zero Flag Logic
endmodule

module half_adder (
  input  input_2,
  input  input_1,
  output S,
  output cout
);

  xor xor_1 (S, input_2, input_1);
  and and_1 (cout, input_2, input_1);
endmodule

module full_adder (
  input  data_1,
  input  data_2,
  input  Cin,
  output sum,
  output cout
);

  wire and_1_out, and_2_out, xor_1_out;

  xor xor_1 (xor_1_out, data_1, data_2);
  and and_1 (and_1_out, data_1, data_2);
  xor xor_2 (sum, xor_1_out, Cin);
  and and_2 (and_2_out, xor_1_out, Cin);
  or or_1 (cout, and_2_out, and_1_out);
endmodule

module _12_bit_adder (
  input  [11:0] input_1,
  input  [11:0] input_2,
  output [11:0] sum
);

  wire full_adder_1_cout, full_adder_2_cout, full_adder_3_cout, full_adder_4_cout, full_adder_5_cout,
       full_adder_6_cout, full_adder_7_cout, full_adder_8_cout, full_adder_9_cout, full_adder_10_cout,
       half_adder_1_cout;

  half_adder half_adder_1 (.input_2(input_2[0]), .input_1(input_1[0]), .S(sum[0]), .cout(half_adder_1_cout));
  full_adder full_adder_1 (
    .data_1(input_2[1]), .data_2(input_1[1]), .Cin(half_adder_1_cout), .sum(sum[1]), .cout(full_adder_1_cout));
  full_adder full_adder_2 (
    .data_1(input_2[2]), .data_2(input_1[2]), .Cin(full_adder_1_cout), .sum(sum[2]), .cout(full_adder_2_cout));
  full_adder full_adder_3 (
    .data_1(input_2[3]), .data_2(input_1[3]), .Cin(full_adder_2_cout), .sum(sum[3]), .cout(full_adder_3_cout));
  full_adder full_adder_4 (
    .data_1(input_2[4]), .data_2(input_1[4]), .Cin(full_adder_3_cout), .sum(sum[4]), .cout(full_adder_4_cout));
  full_adder full_adder_5 (
    .data_1(input_2[5]), .data_2(input_1[5]), .Cin(full_adder_4_cout), .sum(sum[5]), .cout(full_adder_5_cout));
  full_adder full_adder_6 (
    .data_1(input_2[6]), .data_2(input_1[6]), .Cin(full_adder_5_cout), .sum(sum[6]), .cout(full_adder_6_cout));
  full_adder full_adder_7 (
    .data_1(input_2[7]), .data_2(input_1[7]), .Cin(full_adder_6_cout), .sum(sum[7]), .cout(full_adder_7_cout));
  full_adder full_adder_8 (
    .data_1(input_2[8]), .data_2(input_1[8]), .Cin(full_adder_7_cout), .sum(sum[8]), .cout(full_adder_8_cout));
  full_adder full_adder_9 (
    .data_1(input_2[9]), .data_2(input_1[9]), .Cin(full_adder_8_cout), .sum(sum[9]), .cout(full_adder_9_cout));
  full_adder full_adder_10 (
    .data_1(input_2[10]), .data_2(input_1[10]), .Cin(full_adder_9_cout), .sum(sum[10]),
    .cout(full_adder_10_cout));
  full_adder full_adder_11 (
    .data_1(input_2[11]), .data_2(input_1[11]), .Cin(full_adder_10_cout), .sum(sum[11]));  // open: cout
endmodule

module _18_bit_adder (
  input  [17:0] src1,
  input  [17:0] src2,
  output [17:0] out_3,
  output Cout
);

  wire full_adder_1_cout, full_adder_2_cout, full_adder_3_cout, full_adder_4_cout, full_adder_5_cout,
       full_adder_6_cout, full_adder_7_cout, full_adder_8_cout, full_adder_9_cout, full_adder_10_cout,
       full_adder_11_cout, full_adder_12_cout, full_adder_13_cout, full_adder_14_cout, full_adder_15_cout,
       full_adder_16_cout, half_adder_1_cout;

  half_adder half_adder_1 (.input_2(src1[0]), .input_1(src2[0]), .S(out_3[0]), .cout(half_adder_1_cout));
  full_adder full_adder_1 (
    .data_1(src1[1]), .data_2(src2[1]), .Cin(half_adder_1_cout), .sum(out_3[1]), .cout(full_adder_1_cout));
  full_adder full_adder_2 (
    .data_1(src1[2]), .data_2(src2[2]), .Cin(full_adder_1_cout), .sum(out_3[2]), .cout(full_adder_2_cout));
  full_adder full_adder_3 (
    .data_1(src1[3]), .data_2(src2[3]), .Cin(full_adder_2_cout), .sum(out_3[3]), .cout(full_adder_3_cout));
  full_adder full_adder_4 (
    .data_1(src1[4]), .data_2(src2[4]), .Cin(full_adder_3_cout), .sum(out_3[4]), .cout(full_adder_4_cout));
  full_adder full_adder_5 (
    .data_1(src1[5]), .data_2(src2[5]), .Cin(full_adder_4_cout), .sum(out_3[5]), .cout(full_adder_5_cout));
  full_adder full_adder_6 (
    .data_1(src1[6]), .data_2(src2[6]), .Cin(full_adder_5_cout), .sum(out_3[6]), .cout(full_adder_6_cout));
  full_adder full_adder_7 (
    .data_1(src1[7]), .data_2(src2[7]), .Cin(full_adder_6_cout), .sum(out_3[7]), .cout(full_adder_7_cout));
  full_adder full_adder_8 (
    .data_1(src1[8]), .data_2(src2[8]), .Cin(full_adder_7_cout), .sum(out_3[8]), .cout(full_adder_8_cout));
  full_adder full_adder_9 (
    .data_1(src1[9]), .data_2(src2[9]), .Cin(full_adder_8_cout), .sum(out_3[9]), .cout(full_adder_9_cout));
  full_adder full_adder_10 (
    .data_1(src1[10]), .data_2(src2[10]), .Cin(full_adder_9_cout), .sum(out_3[10]), .cout(full_adder_10_cout));
  full_adder full_adder_11 (
    .data_1(src1[11]), .data_2(src2[11]), .Cin(full_adder_10_cout), .sum(out_3[11]), .cout(full_adder_11_cout));
  full_adder full_adder_12 (
    .data_1(src1[12]), .data_2(src2[12]), .Cin(full_adder_11_cout), .sum(out_3[12]), .cout(full_adder_12_cout));
  full_adder full_adder_13 (
    .data_1(src1[13]), .data_2(src2[13]), .Cin(full_adder_12_cout), .sum(out_3[13]), .cout(full_adder_13_cout));
  full_adder full_adder_14 (
    .data_1(src1[14]), .data_2(src2[14]), .Cin(full_adder_13_cout), .sum(out_3[14]), .cout(full_adder_14_cout));
  full_adder full_adder_15 (
    .data_1(src1[15]), .data_2(src2[15]), .Cin(full_adder_14_cout), .sum(out_3[15]), .cout(full_adder_15_cout));
  full_adder full_adder_16 (
    .data_1(src1[16]), .data_2(src2[16]), .Cin(full_adder_15_cout), .sum(out_3[16]), .cout(full_adder_16_cout));
  full_adder full_adder_17 (
    .data_1(src1[17]), .data_2(src2[17]), .Cin(full_adder_16_cout), .sum(out_3[17]), .cout(Cout));
endmodule

module Bcomp (
  input  [17:0] in_1,
  output [17:0] out_2
);

  wire [17:0] not_1_out;

  assign not_1_out = ~in_1;  // NOT_Gate not_1, 18 bits wide
  _18_bit_adder u_18_bit_adder_1 (.src1(not_1_out), .src2(18'h1), .out_3(out_2));  // open: Cout
endmodule

module _18_bit_sub (
  input  [17:0] in_1,
  input  [17:0] in_2,
  output [17:0] out_3,
  output out_4
);

  wire [17:0] bComp_out_2;

  Bcomp bComp (.in_1(in_2), .out_2(bComp_out_2));
  _18_bit_adder _18bit_adder (.src1(in_1), .src2(bComp_out_2), .out_3(out_3), .Cout(out_4));
endmodule

// dfp
module d_flip_flop (
  input  D,
  input  clk,
  output Q
);

  wire master_q_prime, not_1_out;

  not not_1 (not_1_out, clk);
  d_latch master (.D(D), .clk(not_1_out), .Q_prime(master_q_prime));  // open: Q
  d_latch servant (.D(master_q_prime), .clk(clk), .Q(Q));  // open: Q_prime
endmodule

// 18bR
module _18_bit_register (
  input  enable,
  input  clock,
  input  [17:0] register,
  output [17:0] registeroutput
);

  wire and_1_out, and_2_out, and_3_out, and_4_out, and_5_out, and_6_out, and_7_out, and_8_out, and_9_out,
       and_10_out, and_11_out, and_12_out, and_13_out, and_14_out, and_15_out, and_16_out, and_17_out,
       and_18_out;

  and and_1 (and_1_out, enable, clock);
  and and_2 (and_2_out, enable, clock);
  and and_3 (and_3_out, enable, clock);
  and and_4 (and_4_out, enable, clock);
  and and_5 (and_5_out, enable, clock);
  and and_6 (and_6_out, enable, clock);
  and and_7 (and_7_out, enable, clock);
  and and_8 (and_8_out, enable, clock);
  and and_9 (and_9_out, enable, clock);
  and and_10 (and_10_out, enable, clock);
  and and_11 (and_11_out, enable, clock);
  and and_12 (and_12_out, enable, clock);
  and and_13 (and_13_out, enable, clock);
  and and_14 (and_14_out, enable, clock);
  and and_15 (and_15_out, enable, clock);
  and and_16 (and_16_out, enable, clock);
  and and_17 (and_17_out, enable, clock);
  and and_18 (and_18_out, enable, clock);
  d_flip_flop d_flip_flop_1 (.D(register[0]), .clk(and_1_out), .Q(registeroutput[0]));
  d_flip_flop d_flip_flop_2 (.D(register[1]), .clk(and_2_out), .Q(registeroutput[1]));
  d_flip_flop d_flip_flop_3 (.D(register[2]), .clk(and_3_out), .Q(registeroutput[2]));
  d_flip_flop d_flip_flop_4 (.D(register[3]), .clk(and_4_out), .Q(registeroutput[3]));
  d_flip_flop d_flip_flop_5 (.D(register[4]), .clk(and_5_out), .Q(registeroutput[4]));
  d_flip_flop d_flip_flop_6 (.D(register[5]), .clk(and_6_out), .Q(registeroutput[5]));
  d_flip_flop d_flip_flop_7 (.D(register[6]), .clk(and_7_out), .Q(registeroutput[6]));
  d_flip_flop d_flip_flop_8 (.D(register[7]), .clk(and_8_out), .Q(registeroutput[7]));
  d_flip_flop d_flip_flop_9 (.D(register[8]), .clk(and_9_out), .Q(registeroutput[8]));
  d_flip_flop d_flip_flop_10 (.D(register[9]), .clk(and_10_out), .Q(registeroutput[9]));
  d_flip_flop d_flip_flop_11 (.D(register[10]), .clk(and_11_out), .Q(registeroutput[10]));
  d_flip_flop d_flip_flop_12 (.D(register[11]), .clk(and_12_out), .Q(registeroutput[11]));
  d_flip_flop d_flip_flop_13 (.D(register[12]), .clk(and_13_out), .Q(registeroutput[12]));
  d_flip_flop d_flip_flop_14 (.D(register[13]), .clk(and_14_out), .Q(registeroutput[13]));
  d_flip_flop d_flip_flop_15 (.D(register[14]), .clk(and_15_out), .Q(registeroutput[14]));
  d_flip_flop d_flip_flop_16 (.D(register[15]), .clk(and_16_out), .Q(registeroutput[15]));
  d_flip_flop d_flip_flop_17 (.D(register[16]), .clk(and_17_out), .Q(registeroutput[16]));
  d_flip_flop d_flip_flop_18 (.D(register[17]), .clk(and_18_out), .Q(registeroutput[17]));
endmodule

module d_latch (
  input  D,
  input  clk,
  output Q_prime,
  output Q
);

  wire and_1_out, and_2_out, not_1_out;

  and and_1 (and_1_out, D, clk);
  and and_2 (and_2_out, clk, not_1_out);
  not not_1 (not_1_out, D);
  nor nor_1 (Q_prime, and_1_out, Q);
  nor nor_2 (Q, Q_prime, and_2_out);
endmodule

module _12_bit_register (
  input  enable,
  input  clock,
  input  [11:0] in_3,
  output [11:0] out_4
);

  wire and_1_out, and_2_out, and_3_out, and_4_out, and_5_out, and_6_out, and_7_out, and_8_out, and_9_out,
       and_10_out, and_11_out, and_12_out;

  and and_1 (and_1_out, enable, clock);
  and and_2 (and_2_out, enable, clock);
  and and_3 (and_3_out, enable, clock);
  and and_4 (and_4_out, enable, clock);
  and and_5 (and_5_out, enable, clock);
  and and_6 (and_6_out, enable, clock);
  and and_7 (and_7_out, enable, clock);
  and and_8 (and_8_out, enable, clock);
  and and_9 (and_9_out, enable, clock);
  and and_10 (and_10_out, enable, clock);
  and and_11 (and_11_out, enable, clock);
  and and_12 (and_12_out, enable, clock);
  d_flip_flop d_flip_flop_1 (.D(in_3[0]), .clk(and_1_out), .Q(out_4[0]));
  d_flip_flop d_flip_flop_2 (.D(in_3[1]), .clk(and_2_out), .Q(out_4[1]));
  d_flip_flop d_flip_flop_3 (.D(in_3[2]), .clk(and_3_out), .Q(out_4[2]));
  d_flip_flop d_flip_flop_4 (.D(in_3[3]), .clk(and_4_out), .Q(out_4[3]));
  d_flip_flop d_flip_flop_5 (.D(in_3[4]), .clk(and_5_out), .Q(out_4[4]));
  d_flip_flop d_flip_flop_6 (.D(in_3[5]), .clk(and_6_out), .Q(out_4[5]));
  d_flip_flop d_flip_flop_7 (.D(in_3[6]), .clk(and_7_out), .Q(out_4[6]));
  d_flip_flop d_flip_flop_8 (.D(in_3[7]), .clk(and_8_out), .Q(out_4[7]));
  d_flip_flop d_flip_flop_9 (.D(in_3[8]), .clk(and_9_out), .Q(out_4[8]));
  d_flip_flop d_flip_flop_10 (.D(in_3[9]), .clk(and_10_out), .Q(out_4[9]));
  d_flip_flop d_flip_flop_11 (.D(in_3[10]), .clk(and_11_out), .Q(out_4[10]));
  d_flip_flop d_flip_flop_12 (.D(in_3[11]), .clk(and_12_out), .Q(out_4[11]));
endmodule

module ImmExtender (
  input  [17:0] \input ,
  output [17:0] \output 
);

  wire [17:0] bit_extender_1_out, bit_extender_2_out, bit_extender_3_out;

  assign bit_extender_1_out = {{13{\input [4]}}, \input [4:0]};  // Bit_Extender bit_extender_1
  assign bit_extender_2_out = {{9{1'b0}}, \input [8:0]};  // Bit_Extender bit_extender_2
  assign bit_extender_3_out = {{5{\input [12]}}, \input [12:0]};  // Bit_Extender bit_extender_3
  Multiplexer #(.select(2), .width(18)) multiplexer_1 (
    .in0(bit_extender_1_out), .in1(bit_extender_2_out), .in2(bit_extender_3_out),
    .in3({\input [8:0], {9{1'b0}}}), .out(\output ), .sel(2'b00));  // open: en

  // Notes on the sheet:
  //   ADDI result
  //   LD/ST result
  //   JUMP result
  //   LUI result
endmodule

module Control_Unit (
  input  [4:0] Opcode,
  input  Zero,
  input  Clock,
  input  Reset,
  output PCWrite,
  output IRWrite,
  output RegWrite,
  output MemWrite,
  output MemToReg,
  output ALUSrc,
  output RegDst,
  output PCSrc,
  output [2:0] ALUOp
);

  wire [3:0] logic_nextstate_1_next0, SR_q;

  Logic_NextState logic_nextstate_1 (
    .S3(SR_q[3]), .S2(SR_q[2]), .S1(SR_q[1]), .S0(SR_q[0]), .Op4(Opcode[4]), .Op3(Opcode[3]),
    .Op2(Opcode[2]), .Op1(Opcode[1]), .Op0(Opcode[0]), .Zero(Zero), .Next3(logic_nextstate_1_next0[3]),
    .Next2(logic_nextstate_1_next0[2]), .Next1(logic_nextstate_1_next0[1]), .Next0(logic_nextstate_1_next0[0]));
  Register #(.width(4)) SR (.D(logic_nextstate_1_next0), .Q(SR_q), .clk(Clock), .clr(Reset));  // open: en
  Logic_Signals logic_signals_1 (
    .S3(SR_q[3]), .S2(SR_q[2]), .S1(SR_q[1]), .S0(SR_q[0]), .Op4(Opcode[4]), .Op3(Opcode[3]),
    .Op2(Opcode[2]), .Op1(Opcode[1]), .Op0(Opcode[0]), .Zero(Zero), .PCWrite(PCWrite), .IRWrite(IRWrite),
    .RegWrite(RegWrite), .MemWrite(MemWrite), .MemToReg(MemToReg), .ALUSrc(ALUSrc), .RegDst(RegDst),
    .PCSrc(PCSrc), .ALU2(ALUOp[2]), .ALU1(ALUOp[1]), .ALU0(ALUOp[0]));
endmodule

// next state
module Logic_NextState (
  input  S3,
  input  S2,
  input  S1,
  input  S0,
  input  Op4,
  input  Op3,
  input  Op2,
  input  Op1,
  input  Op0,
  input  Zero,
  output Next3,
  output Next2,
  output Next1,
  output Next0
);

  wire and_1_out, and_2_out, and_3_out, and_4_out, and_5_out, and_6_out, and_7_out, and_8_out, and_9_out,
       and_10_out, and_11_out, and_12_out, and_13_out, and_14_out, and_15_out, not_1_out, not_2_out,
       not_3_out, not_4_out, not_5_out, not_6_out, not_7_out, not_8_out, not_9_out, not_10_out, not_11_out,
       not_12_out, not_13_out, not_14_out, not_15_out, not_16_out, not_17_out, not_18_out, not_19_out,
       not_20_out, not_21_out, not_22_out, not_23_out, not_24_out, not_25_out, not_26_out, not_27_out,
       not_28_out, not_29_out, not_30_out, not_31_out, not_32_out, not_33_out, not_34_out, not_35_out,
       not_36_out, not_37_out, not_38_out, not_39_out, not_40_out, not_41_out, not_42_out, not_43_out,
       not_44_out, not_45_out, not_46_out, not_47_out, not_48_out, not_49_out, not_50_out, not_51_out,
       not_52_out, not_53_out, not_54_out, not_55_out, not_56_out, not_57_out, not_58_out, not_59_out,
       not_60_out, not_61_out;

  not not_1 (not_1_out, S3);
  not not_2 (not_2_out, S2);
  not not_3 (not_3_out, S1);
  not not_4 (not_4_out, Op4);
  not not_5 (not_5_out, Op2);
  not not_6 (not_6_out, S3);
  not not_7 (not_7_out, S2);
  not not_8 (not_8_out, S1);
  not not_9 (not_9_out, Op4);
  not not_10 (not_10_out, Op1);
  not not_11 (not_11_out, S3);
  not not_12 (not_12_out, S1);
  not not_13 (not_13_out, S0);
  not not_14 (not_14_out, S3);
  not not_15 (not_15_out, S2);
  not not_16 (not_16_out, S1);
  not not_17 (not_17_out, Op3);
  not not_18 (not_18_out, S3);
  not not_19 (not_19_out, S2);
  not not_20 (not_20_out, S1);
  not not_21 (not_21_out, Op2);
  not not_22 (not_22_out, Op1);
  not not_23 (not_23_out, S3);
  not not_24 (not_24_out, S2);
  not not_25 (not_25_out, S1);
  not not_26 (not_26_out, Op1);
  not not_27 (not_27_out, S3);
  not not_28 (not_28_out, S2);
  not not_29 (not_29_out, S1);
  not not_30 (not_30_out, S3);
  not not_31 (not_31_out, S2);
  not not_32 (not_32_out, S1);
  not not_33 (not_33_out, S3);
  not not_34 (not_34_out, S2);
  not not_35 (not_35_out, S0);
  not not_36 (not_36_out, S3);
  not not_37 (not_37_out, S1);
  not not_38 (not_38_out, Op4);
  not not_39 (not_39_out, Op2);
  not not_40 (not_40_out, Op0);
  not not_41 (not_41_out, S3);
  not not_42 (not_42_out, S1);
  not not_43 (not_43_out, Op4);
  not not_44 (not_44_out, Op1);
  not not_45 (not_45_out, Op0);
  not not_46 (not_46_out, S3);
  not not_47 (not_47_out, S2);
  not not_48 (not_48_out, S0);
  not not_49 (not_49_out, S3);
  not not_50 (not_50_out, S1);
  not not_51 (not_51_out, S0);
  not not_52 (not_52_out, S3);
  not not_53 (not_53_out, S1);
  not not_54 (not_54_out, Op4);
  not not_55 (not_55_out, Op2);
  not not_56 (not_56_out, Op0);
  not not_57 (not_57_out, S3);
  not not_58 (not_58_out, S1);
  not not_59 (not_59_out, Op4);
  not not_60 (not_60_out, Op1);
  not not_61 (not_61_out, Op0);
  and and_1 (and_1_out, not_1_out, not_2_out, not_3_out, S0, not_4_out, Op3, not_5_out, Op1);
  and and_2 (and_2_out, not_6_out, not_7_out, not_8_out, S0, not_9_out, Op3, Op2, not_10_out);
  and and_3 (and_3_out, not_11_out, S2, not_12_out, not_13_out);
  and and_4 (and_4_out, not_14_out, not_15_out, not_16_out, S0, not_17_out);
  and and_5 (and_5_out, not_18_out, not_19_out, not_20_out, S0, not_21_out, not_22_out);
  and and_6 (and_6_out, not_23_out, not_24_out, not_25_out, S0, not_26_out, Op0);
  and and_7 (and_7_out, not_27_out, not_28_out, not_29_out, S0, Op2, Op1);
  and and_8 (and_8_out, not_30_out, not_31_out, not_32_out, S0, Op4);
  and and_9 (and_9_out, not_33_out, not_34_out, S1, not_35_out);
  and and_10 (and_10_out, not_36_out, S2, not_37_out, S0, not_38_out, Op3, not_39_out, Op1, not_40_out);
  and and_11 (and_11_out, not_41_out, S2, not_42_out, S0, not_43_out, Op3, Op2, not_44_out, not_45_out);
  and and_12 (and_12_out, not_46_out, not_47_out, not_48_out);
  and and_13 (and_13_out, not_49_out, not_50_out, not_51_out);
  and and_14 (and_14_out, not_52_out, S2, not_53_out, not_54_out, Op3, not_55_out, Op1, not_56_out);
  and and_15 (and_15_out, not_57_out, S2, not_58_out, not_59_out, Op3, Op2, not_60_out, not_61_out);
  or or_1 (Next2, and_1_out, and_2_out, and_3_out);
  or or_2 (Next0, and_12_out, and_13_out, and_14_out, and_15_out);
  or or_3 (Next1, and_4_out, and_5_out, and_6_out, and_7_out, and_8_out, and_9_out, and_10_out, and_11_out);

  assign Next3 = 1'b0;
endmodule

// signals
module Logic_Signals (
  input  S3,
  input  S2,
  input  S1,
  input  S0,
  input  Op4,
  input  Op3,
  input  Op2,
  input  Op1,
  input  Op0,
  input  Zero,
  output PCWrite,
  output IRWrite,
  output RegWrite,
  output MemWrite,
  output MemToReg,
  output ALUSrc,
  output RegDst,
  output PCSrc,
  output ALU2,
  output ALU1,
  output ALU0
);

  wire and_2_out, and_3_out, and_5_out, and_6_out, and_7_out, and_8_out, and_9_out, and_10_out, and_11_out,
       and_13_out, and_14_out, and_15_out, and_16_out, and_17_out, and_18_out, and_19_out, and_20_out,
       and_21_out, and_22_out, and_23_out, and_25_out, and_26_out, and_27_out, and_28_out, and_29_out,
       and_30_out, and_31_out, and_32_out, not_1_out, not_2_out, not_3_out, not_4_out, not_5_out, not_6_out,
       not_7_out, not_8_out, not_9_out, not_10_out, not_11_out, not_12_out, not_13_out, not_14_out,
       not_15_out, not_16_out, not_17_out, not_18_out, not_19_out, not_20_out, not_21_out, not_22_out,
       not_23_out, not_24_out, not_25_out, not_26_out, not_27_out, not_28_out, not_29_out, not_30_out,
       not_31_out, not_32_out, not_33_out, not_34_out, not_35_out, not_36_out, not_37_out, not_38_out,
       not_39_out, not_40_out, not_41_out, not_42_out, not_43_out, not_44_out, not_45_out, not_46_out,
       not_47_out, not_48_out, not_49_out, not_50_out, not_51_out, not_52_out, not_53_out, not_54_out,
       not_55_out, not_56_out, not_57_out, not_58_out, not_59_out, not_60_out, not_61_out, not_62_out,
       not_63_out, not_64_out, not_65_out, not_66_out, not_67_out, not_68_out, not_69_out, not_70_out,
       not_71_out, not_72_out, not_73_out, not_74_out;

  not not_1 (not_1_out, S2);
  not not_2 (not_2_out, S1);
  not not_3 (not_3_out, S0);
  not not_4 (not_4_out, S2);
  not not_5 (not_5_out, S1);
  not not_6 (not_6_out, S0);
  not not_7 (not_7_out, S2);
  not not_8 (not_8_out, Op3);
  not not_9 (not_9_out, Op2);
  not not_10 (not_10_out, Op1);
  not not_11 (not_11_out, Op0);
  not not_12 (not_12_out, Op4);
  not not_13 (not_13_out, Op1);
  not not_14 (not_14_out, Op4);
  not not_15 (not_15_out, Op2);
  not not_16 (not_16_out, S3);
  not not_17 (not_17_out, S2);
  not not_18 (not_18_out, Op4);
  not not_19 (not_19_out, Op1);
  not not_20 (not_20_out, Op0);
  not not_21 (not_21_out, Op4);
  not not_22 (not_22_out, Op3);
  not not_23 (not_23_out, Op4);
  not not_24 (not_24_out, Op2);
  not not_25 (not_25_out, Op1);
  not not_26 (not_26_out, Op4);
  not not_27 (not_27_out, Op4);
  not not_28 (not_28_out, Op3);
  not not_29 (not_29_out, Op4);
  not not_30 (not_30_out, Op2);
  not not_31 (not_31_out, Op1);
  not not_32 (not_32_out, Op4);
  not not_33 (not_33_out, S2);
  not not_34 (not_34_out, S0);
  not not_35 (not_35_out, Op3);
  not not_36 (not_36_out, S2);
  not not_37 (not_37_out, S0);
  not not_38 (not_38_out, Op2);
  not not_39 (not_39_out, S2);
  not not_40 (not_40_out, S0);
  not not_41 (not_41_out, Op0);
  not not_42 (not_42_out, S1);
  not not_43 (not_43_out, S0);
  not not_44 (not_44_out, Op4);
  not not_45 (not_45_out, Op1);
  and and_1 (PCSrc, S2, S1);
  not not_46 (not_46_out, S2);
  not not_47 (not_47_out, S0);
  not not_48 (not_48_out, Op3);
  not not_49 (not_49_out, Op1);
  not not_50 (not_50_out, S2);
  not not_51 (not_51_out, S0);
  not not_52 (not_52_out, Op0);
  not not_53 (not_53_out, S2);
  not not_54 (not_54_out, Op3);
  not not_55 (not_55_out, Op1);
  not not_56 (not_56_out, Zero);
  not not_57 (not_57_out, S2);
  not not_58 (not_58_out, S0);
  not not_59 (not_59_out, Op3);
  not not_60 (not_60_out, Op2);
  not not_61 (not_61_out, S2);
  not not_62 (not_62_out, S0);
  not not_63 (not_63_out, Op2);
  not not_64 (not_64_out, Op1);
  not not_65 (not_65_out, S2);
  not not_66 (not_66_out, S0);
  not not_67 (not_67_out, Op0);
  not not_68 (not_68_out, S2);
  not not_69 (not_69_out, S0);
  not not_70 (not_70_out, Op3);
  not not_71 (not_71_out, S2);
  not not_72 (not_72_out, S0);
  not not_73 (not_73_out, Op2);
  not not_74 (not_74_out, Op1);
  and and_2 (and_2_out, not_1_out, not_2_out, not_3_out);
  and and_3 (and_3_out, S2, S1);
  and and_4 (IRWrite, not_4_out, not_5_out, not_6_out);
  and and_5 (and_5_out, not_7_out, S1, Op4);
  and and_6 (and_6_out, S1, S0, not_8_out);
  and and_7 (and_7_out, S1, S0, not_9_out);
  and and_8 (and_8_out, S1, S0, not_10_out);
  and and_9 (and_9_out, S1, S0, not_11_out);
  and and_10 (and_10_out, S1, S0, Zero);
  and and_11 (and_11_out, S2, S1, not_12_out, Op3, Op2, not_13_out, Op0);
  and and_12 (MemWrite, S2, S0, not_14_out, Op3, not_15_out, Op1, Op0);
  and and_13 (and_13_out, not_16_out, not_17_out, S1, S0, not_18_out, Op3, Op2, not_19_out, not_20_out);
  and and_14 (and_14_out, S2, S1, S0, not_21_out, not_22_out);
  and and_15 (and_15_out, S2, S1, S0, not_23_out, not_24_out, not_25_out);
  and and_16 (and_16_out, S2, S1, S0, not_26_out, Op2, Op1);
  and and_17 (and_17_out, S3, S1, S0, not_27_out, not_28_out);
  and and_18 (and_18_out, S3, S1, S0, not_29_out, not_30_out, not_31_out);
  and and_19 (and_19_out, S3, S1, S0, not_32_out, Op2, Op1);
  and and_20 (and_20_out, not_33_out, S1, not_34_out, not_35_out, Op2, Op1);
  and and_21 (and_21_out, not_36_out, S1, not_37_out, Op3, not_38_out, Op1);
  and and_22 (and_22_out, not_39_out, S1, not_40_out, Op3, Op1, not_41_out);
  and and_23 (and_23_out, S2, not_42_out, not_43_out);
  and and_24 (RegDst, S2, S1, not_44_out, Op3, Op2, not_45_out, Op0);
  and and_25 (and_25_out, not_46_out, S1, not_47_out, not_48_out, Op2, not_49_out);
  and and_26 (and_26_out, not_50_out, S1, not_51_out, Op3, Op2, Op1, not_52_out);
  and and_27 (and_27_out, not_53_out, S1, Op4, not_54_out, Op2, not_55_out, Op0, not_56_out);
  and and_28 (and_28_out, not_57_out, S1, not_58_out, not_59_out, not_60_out, Op1);
  and and_29 (and_29_out, not_61_out, S1, not_62_out, Op3, not_63_out, not_64_out);
  and and_30 (and_30_out, not_65_out, S1, not_66_out, Op3, Op2, Op1, not_67_out);
  and and_31 (and_31_out, not_68_out, S1, not_69_out, not_70_out, Op0);
  and and_32 (and_32_out, not_71_out, S1, not_72_out, not_73_out, not_74_out, Op0);
  or or_1 (PCWrite, and_2_out, and_3_out);
  or or_2 (RegWrite, and_5_out, and_6_out, and_7_out, and_8_out, and_9_out, and_10_out, and_11_out);
  or or_3 (MemToReg, and_13_out, and_14_out, and_15_out, and_16_out, and_17_out, and_18_out, and_19_out);
  or or_4 (ALUSrc, and_20_out, and_21_out, and_22_out, and_23_out);
  or or_5 (ALU2, and_25_out, and_26_out, and_27_out);
  or or_6 (ALU1, and_28_out, and_29_out, and_30_out);
  or or_7 (ALU0, and_31_out, and_32_out);
endmodule

module RegisterFile_test (
  input  [3:0] in_1,
  input  [3:0] in_2,
  input  [17:0] in_3,
  input  [3:0] in_4,
  input  in_5,
  input  in_6,
  output [17:0] out_7,
  output [17:0] out_8
);

  wire [17:0] register_file_1_r0, register_file_1_r1, register_file_1_r2, register_file_1_r3,
       register_file_1_r4, register_file_1_r5, register_file_1_r6, register_file_1_r7, register_file_1_r8,
       register_file_1_r9, register_file_1_r10, register_file_1_r11, register_file_1_r12,
       register_file_1_r13, register_file_1_r14, register_file_1_r15;

  Register_File register_file_1 (
    .R0(register_file_1_r0), .R1(register_file_1_r1), .R2(register_file_1_r2), .rReg1(in_1),
    .R3(register_file_1_r3), .oData1(out_7), .R4(register_file_1_r4), .R5(register_file_1_r5),
    .oData2(out_8), .R6(register_file_1_r6), .rReg2(in_2), .wData(in_3), .R7(register_file_1_r7),
    .R8(register_file_1_r8), .R9(register_file_1_r9), .R10(register_file_1_r10), .wReg(in_4),
    .R11(register_file_1_r11), .R12(register_file_1_r12), .R13(register_file_1_r13),
    .R14(register_file_1_r14), .R15(register_file_1_r15), .WE(in_5), .Clock(in_6));  // open: reset
  // Probe on register_file_1_r0
  // Probe on register_file_1_r1
  // Probe on register_file_1_r2
  // Probe on register_file_1_r3
  // Probe on register_file_1_r4
  // Probe on register_file_1_r5
  // Probe on register_file_1_r6
  // Probe on register_file_1_r7
  // Probe on register_file_1_r8
  // Probe on register_file_1_r9
  // Probe on register_file_1_r10
  // Probe on register_file_1_r11
  // Probe on register_file_1_r12
  // Probe on register_file_1_r13
  // Probe on register_file_1_r14
  // Probe on register_file_1_r15
endmodule
